// Logisim project maxterms circuito combinacional.circ as structural Verilog: 1 circuit, main circuit main
module main (
  input  A,
  input  B,
  input  C,
  input  D,
  output out_5,
  output out_6,
  output out_7,
  output out_8
);

  wire not_1_out, not_2_out, not_3_out, not_4_out, or_1_out, or_2_out, or_3_out, or_4_out, or_5_out,
       or_6_out, or_7_out, or_8_out, or_9_out;

  not not_1 (not_1_out, A);
  not not_2 (not_2_out, C);
  not not_3 (not_3_out, B);
  not not_4 (not_4_out, D);
  or or_1 (or_1_out, not_2_out, not_3_out);
  or or_2 (or_2_out, A, B);
  or or_3 (or_3_out, not_3_out, C);
  or or_4 (or_4_out, not_1_out, not_2_out);
  or or_5 (or_5_out, B, C);
  or or_6 (or_6_out, A, B);
  or or_7 (or_7_out, A, C);
  or or_8 (or_8_out, not_1_out, not_3_out, not_4_out);
  or or_9 (or_9_out, not_1_out, not_2_out, not_4_out);
  and and_1 (out_5, not_1_out, or_1_out);
  and and_2 (out_6, or_2_out, or_3_out, or_4_out, not_4_out);
  and and_3 (out_7, A, or_5_out);
  and and_4 (out_8, or_6_out, or_7_out, or_8_out, or_9_out);

  // Notes on the sheet:
  //   FUNCION LED ROJO
  //   FUNCION LED AMARILLO
  //   FUNCION LED VERDE
  //   FUNCION SONORA PARA INVIDENTES
endmodule
